# Fritzing sketch schematic (saved by Fritzing 0.9.4)
breadboards: 1

parts:
  Raspberry_Pi_5_8GB = Raspberry Pi B+
  MCP3008 = MCP3008 [package=dil16]  # not connected
  IR1 = TSOP312.., 314.. [package=THT]  # not connected
  D2 = SOLAR-IXYS [package=solarbit-12x1]  # not connected
  Powerbank_5V = BC9VPC [package=bc9vpc]
  INA1 = INA219 DC Current Sensor Breakout
  RFID = RFID-RC522-v2
  LED1 = LEDs [package=led10mm]
  LED2 = LEDs [package=led10mm]
  LED4 = LEDs [package=led10mm]
  LED_3 = LEDs [package=led10mm]
  M1 = DC Motor
  LED5 = LEDs [package=led10mm]
  INA2 = INA219 DC Current Sensor Breakout
  INA3 = INA219 DC Current Sensor Breakout
  INA4 = INA219 DC Current Sensor Breakout
  R7/Heating_pad = Resistor [tolerance=±5% resistance=10 package="2512 [SMD]"]
  Q1_SS8050 = TRANSISTOR_NPN [package=to-92]
  Q2_SS8050 = TRANSISTOR_NPN [package=to-92]
  5V_TO_3V3 = Transformer [package=transformer_smd]
  R6 = Resistor [tolerance=±5% resistance=470 package="2512 [SMD]"]
  R5 = Resistor [tolerance=±5% resistance=470 package="2512 [SMD]"]
  R1 = Resistor [tolerance=±5% resistance=100 package="0805 [SMD]"]
  R3 = Resistor [tolerance=±5% resistance=100 package="0805 [SMD]"]
  R2 = Resistor [tolerance=±5% resistance=100 package="0805 [SMD]"]
  D1 = Rectifier Diode [package="Melf DO-213 AA [SMD]"]
  R8/Heating_pad = Resistor [tolerance=±5% resistance=10 package="2512 [SMD]"]
  R4 = Resistor [tolerance=±5% resistance=100 package="0805 [SMD]"]
  Q3_2N2222A = TRANSISTOR_NPN [package=to-92]
  Q4_2N2222A = TRANSISTOR_NPN [package=to-92]
  R9 = Resistor [tolerance=±5% resistance=2k package="2512 [SMD]"]
  R10 = Resistor [tolerance=±5% resistance=2k package="2512 [SMD]"]
  Q5_2N2222A = TRANSISTOR_NPN [package=to-92]
  R11 = Resistor [tolerance=±5% resistance=5.1k package="2512 [SMD]"]
  L1_SOLENOIDE_LOCK = Solenoid
  D3 = Rectifier Diode [package="Melf DO-213 AA [SMD]"]
  Q5_TIP120 = TRANSISTOR_NPN [package=to-92]
  R12 = Resistor [tolerance=±5% resistance=470k package="2512 [SMD]"]

nets:
  N1: Raspberry_Pi_5_8GB.GPIO2, INA1.SDA, INA2.SDA, INA3.SDA, INA4.SDA
  N2: Raspberry_Pi_5_8GB.GPIO3, INA1.SCL, INA2.SCL, INA3.SCL, INA4.SCL
  N3: Raspberry_Pi_5_8GB.GPIO10, RFID.MOSI
  N4: Raspberry_Pi_5_8GB.GPIO9, RFID.MISO
  N5: Raspberry_Pi_5_8GB.GPIO11, RFID.SCK
  GND: Raspberry_Pi_5_8GB.GND, Powerbank_5V.V-, INA1.GND, INA2.GND, INA3.GND, INA4.GND, Q2_SS8050.E, 5V_TO_3V3.2, 5V_TO_3V3.4
  N6: Raspberry_Pi_5_8GB.GPIO21, R12.Pin_0
  N7: Raspberry_Pi_5_8GB.GPIO20, R11.Pin_0
  N8: Raspberry_Pi_5_8GB.GPIO16, R6.Pin_0
  N9: Raspberry_Pi_5_8GB.GPIO12, R5.Pin_0
  N10: Raspberry_Pi_5_8GB.GPIO7, RFID.SDA
  N11: Raspberry_Pi_5_8GB.GPIO25, R10.Pin_0
  N12: Raspberry_Pi_5_8GB.GPIO24, R9.Pin_0
  N13: Powerbank_5V.V+, INA1.Vin+, LED5.A, INA2.Vin+, INA3.Vin+, INA4.Vin+, 5V_TO_3V3.1, L1_SOLENOIDE_LOCK.pin1, D3.cathode
  VCC: INA1.VCC, INA2.VCC, INA3.VCC, INA4.VCC, 5V_TO_3V3.3
  N14: LED1.C, R1.Pin_0
  N15: LED1.A, LED2.A
  N16: LED2.C, R2.Pin_0
  N17: LED4.C, R3.Pin_0
  N18: LED4.A, LED_3.A, INA2.Vin-
  N19: LED_3.C, R4.Pin_0
  N20: M1.pin_1, INA3.Vin-, D1.cathode
  N21: M1.pin_2, Q1_SS8050.C, D1.anode
  N22: LED5.C, Q5_2N2222A.C
  N23: INA4.Vin-, R7/Heating_pad.Pin_0, R8/Heating_pad.Pin_0
  N24: R7/Heating_pad.Pin_1, Q2_SS8050.C, R8/Heating_pad.Pin_1
  N25: Q1_SS8050.E, Q3_2N2222A.E, Q4_2N2222A.E, Q5_2N2222A.E, Q5_TIP120.E
  N26: Q1_SS8050.B, R5.Pin_1
  N27: Q2_SS8050.B, R6.Pin_1
  N28: R1.Pin_1, R2.Pin_1, Q4_2N2222A.C
  N29: R3.Pin_1, R4.Pin_1, Q3_2N2222A.C
  N30: Q3_2N2222A.B, R10.Pin_1
  N31: Q4_2N2222A.B, R9.Pin_1
  N32: Q5_2N2222A.B, R11.Pin_1
  N33: L1_SOLENOIDE_LOCK.pin2, D3.anode, Q5_TIP120.C
  N34: Q5_TIP120.B, R12.Pin_1

custom parts:
  INA219 DC Current Sensor Breakout: INA DC Current Sensor Breakout
  RFID-RC522-v2: A simple China made RFID-RC522 Reader; do check the pin labels, as this is a MFRC522 based clone.
